// Logisim project tty.circ as structural Verilog: 1 circuit, main circuit main
module main (
);

  wire and_2_out, CLKOUT, clr_2_out, clr_3_out, clr_4_out, clr_out, comparator_1_eq, not_1_out,
       pic16f84a_1_p8, s_r_ff_1_q, s_r_ff_1_qn;
  wire [0:0] and_1_out;
  wire [4:0] pic16f84a_1_p1;
  wire [6:0] controlled_buffer_1_out, Shift_reg_out, Shift_reg_q0, Shift_reg_q1, Shift_reg_q2, Shift_reg_q3,
       undriven;
  wire [7:0] keyboard_1_data, multiplexer_1_out, multiplexer_2_out;
  wire [7:7] pic16f84a_1_p1_2;

  Keyboard #(.trigger("falling")) keyboard_1 (
    .clk(CLKOUT), .re(s_r_ff_1_qn), .clr(clr_out), .avail(keyboard_1_data[7]), .data(keyboard_1_data[6:0]));
  Button clr (.out(clr_out));
  and and_1 (and_1_out[0], s_r_ff_1_qn, keyboard_1_data[7]);
  Multiplexer #(.width(8), .enable("false")) multiplexer_1 (
    .in0({keyboard_1_data[6:0], and_1_out[0]}), .in1({undriven, pic16f84a_1_p1[2]}), .out(multiplexer_1_out),
    .sel(pic16f84a_1_p1[2]));
  // Probe on multiplexer_1_out[7:1]
  TTY #(.trigger("falling")) tty_1 (
    .data(multiplexer_1_out[7:1]), .clk(CLKOUT), .we(multiplexer_1_out[0]), .clr(clr_2_out));
  Button clr_2 (.out(clr_2_out));
  // Probe on keyboard_1_data[6:0]
  Comparator #(.width(7)) comparator_1 (
    .a(7'b0001010), .b(keyboard_1_data[6:0]), .eq(comparator_1_eq));  // open: gt, lt
  Shift_Register #(.width(7), .length(4), .trigger("falling")) Shift_reg (
    .shift(multiplexer_2_out[7]), .in(multiplexer_2_out[6:0]), .clk(CLKOUT), .out(Shift_reg_out),
    .clr(clr_3_out), .q0(Shift_reg_q0), .q1(Shift_reg_q1), .q2(Shift_reg_q2), .q3(Shift_reg_q3));  // open: load, d0, d1, d2, d3
  Multiplexer #(.width(8), .enable("false")) multiplexer_2 (
    .in0({pic16f84a_1_p1_2[7], {7{1'b0}}}), .in1(keyboard_1_data), .out(multiplexer_2_out), .sel(s_r_ff_1_qn));
  Button clr_3 (.out(clr_3_out));
  and and_2 (and_2_out, comparator_1_eq, not_1_out);
  not not_1 (not_1_out, pic16f84a_1_p1[3]);
  // Probe on Shift_reg_q2
  // Probe on Shift_reg_q0
  // Probe on Shift_reg_q3
  // Probe on Shift_reg_q1
  S_R_Flip_Flop s_r_ff_1 (
    .S(and_2_out), .clk(CLKOUT), .R(pic16f84a_1_p1[3]), .Q(s_r_ff_1_q), .Qn(s_r_ff_1_qn), .reset(clr_4_out));  // open: preset, en
  Button clr_4 (.out(clr_4_out));
  assign controlled_buffer_1_out = pic16f84a_1_p1_2[7] ? Shift_reg_out : 7'bz;  // Controlled_Buffer controlled_buffer_1
  Clock clock_1 ();  // open: out
  // Probe on pic16f84a_1_p1[3]
  Button button_1 ();  // open: out
  Button button_2 ();  // open: out
  // Probe on pic16f84a_1_p1_2[7]
  // Probe on s_r_ff_1_q
  // Probe on controlled_buffer_1_out
  // Probe on undriven
  // Probe on pic16f84a_1_p1[2]
  Button button_3 ();  // open: out
  // PIC16F84A pic16f84a_1: pin names not known; wires that end beside it: {pic16f84a_1_p1[4:2], pic16f84a_1_p1_2[7], pic16f84a_1_p1[0]}, s_r_ff_1_q, controlled_buffer_1_out[6], controlled_buffer_1_out[5], controlled_buffer_1_out[4], controlled_buffer_1_out[3:1], CLKOUT, pic16f84a_1_p8
  // Probe on nothing
  Button MCLR (.out(pic16f84a_1_p8));

  // Notes on the sheet:
  //   keyboard
  //   enable write keyboard+shift to screen
  //   write  byte to PORTB
endmodule
